// Logisim project RISC-V.circ as structural Verilog: 8 circuits, main circuit main
module main (
  input  in_1
);

  wire and_1_out, and_2_out, AUIPC, branch_evaluator_out_4, clock_1_out, comparator_1_eq, comparator_2_eq,
       comparator_3_eq, comparator_4_eq, JAL, JALR, LUI, not_1_out, not_2_out, not_3_out, not_4_out,
       not_5_out, not_6_out, not_7_out, not_8_out, or_1_out, or_2_out, register_write_1_out_2;
  wire [2:0] funct3;
  wire [4:0] immediate_decoder_1_rd, immediate_decoder_1_rs1, immediate_decoder_1_rs2, multiplexer_1_out,
       multiplexer_2_out;
  wire [6:0] funct7, opcode;
  wire [11:0] immediate_decoder_1_i;
  wire [12:0] immediate_decoder_1_b;
  wire [19:0] immediate_decoder_1_u;
  wire [23:0] bit_extender_3_out, counter_1_q, transistor_1_out_2;
  wire [31:0] adder_1_out, adder_2_out, adder_3_out, adder_4_out, adder_5_out, ALU_out_6, bit_extender_1_out,
       I_immediate_32b, immediate_decoder_1_j, multiplexer_3_out, multiplexer_4_out, multiplexer_5_out,
       multiplexer_6_out, multiplexer_7_out, multiplexer_8_out, ram_1_data, ram_2_data, register_1_q,
       register_2_q, rom_1_data, transistor_1_out;

  Clock clock_1 (.out(clock_1_out));
  and and_1 (and_1_out, clock_1_out, not_1_out);
  not not_1 (not_1_out, not_2_out);
  not not_2 (not_2_out, clock_1_out);
  Transistor #(.\type ("n"), .gate("br"), .width(32)) transistor_1 (
    .in(32'h10074), .out({transistor_1_out[31:26], transistor_1_out_2, transistor_1_out[1:0]}), .gate(in_1));
  immediate_chooser immediate_chooser_1 (.opcode(opcode), .funct3(funct3));  // open: I, R, S, B, U, J
  Transistor #(.\type ("n"), .gate("br"), .width(32)) transistor_2 (
    .in(adder_5_out), .out({transistor_1_out[31:26], transistor_1_out_2, transistor_1_out[1:0]}), .gate(JALR));
  Counter #(.width(24), .max('hffffff), .trigger("falling")) counter_1 (
    .load(or_1_out), .D(transistor_1_out_2), .count(not_3_out), .Q(counter_1_q), .clk(and_1_out));  // open: carry, clr
  not not_3 (not_3_out, or_1_out);
  or or_1 (or_1_out, in_1, and_2_out, JAL, JALR);
  Transistor #(.\type ("n"), .gate("br"), .width(32)) transistor_3 (
    .in(adder_2_out), .out({transistor_1_out[31:26], transistor_1_out_2, transistor_1_out[1:0]}), .gate(JAL));
  not not_4 (not_4_out, clock_1_out);
  Transistor #(.\type ("n"), .gate("br"), .width(32)) transistor_4 (
    .in(adder_1_out), .out({transistor_1_out[31:26], transistor_1_out_2, transistor_1_out[1:0]}),
    .gate(and_2_out));
  LUI_AUIPC_JAL_JALR lui_auipc_jal_jalr_1 (.in_1(opcode), .JALR(JALR), .JAL(JAL), .AUIPC(AUIPC), .LUI(LUI));
  ROM #(.addrWidth(24), .dataWidth(32)) rom_1 (.addr(counter_1_q), .data(rom_1_data));  // open: sel
  assign bit_extender_1_out = {{19{immediate_decoder_1_b[12]}}, immediate_decoder_1_b};  // Bit_Extender bit_extender_1
  Adder #(.width(32)) adder_1 (
    .a(bit_extender_1_out), .b({{6{1'b0}}, counter_1_q, 2'b00}), .out(adder_1_out));  // open: cin, cout
  Adder #(.width(32)) adder_2 (
    .a(immediate_decoder_1_j), .b({{6{1'b0}}, counter_1_q, 2'b00}), .out(adder_2_out));  // open: cin, cout
  immediate_decoder immediate_decoder_1 (
    .in_1(rom_1_data), .rd(immediate_decoder_1_rd), .rs1(immediate_decoder_1_rs1),
    .rs2(immediate_decoder_1_rs2), .funct3(funct3), .funct7(funct7), .I(immediate_decoder_1_i),
    .B(immediate_decoder_1_b), .U(immediate_decoder_1_u), .J(immediate_decoder_1_j), .opcode(opcode));  // open: S
  assign I_immediate_32b = {{20{immediate_decoder_1_i[11]}}, immediate_decoder_1_i};  // Bit_Extender bit_extender_2
  Adder #(.width(32)) adder_3 (
    .a({immediate_decoder_1_u, {12{1'b0}}}), .b({{6{1'b0}}, counter_1_q, 2'b00}), .out(adder_3_out));  // open: cin, cout
  Adder #(.width(32)) adder_4 (.a({{6{1'b0}}, counter_1_q, 2'b00}), .b(32'h4), .out(adder_4_out));  // open: cin, cout
  Adder #(.width(32)) adder_5 (.a(register_1_q), .b(I_immediate_32b), .out(adder_5_out));  // open: cin, cout
  not not_5 (not_5_out, and_1_out);
  not not_6 (not_6_out, not_5_out);
  not not_7 (not_7_out, not_6_out);
  not not_8 (not_8_out, not_7_out);
  Multiplexer #(.width(5)) multiplexer_1 (
    .in0(immediate_decoder_1_rs1), .in1(immediate_decoder_1_rd), .out(multiplexer_1_out), .sel(and_1_out));  // open: en
  Multiplexer #(.width(5)) multiplexer_2 (
    .in0(immediate_decoder_1_rs2), .in1(immediate_decoder_1_rd), .out(multiplexer_2_out), .sel(and_1_out));  // open: en
  Multiplexer #(.width(32)) multiplexer_3 (
    .in0(multiplexer_4_out), .in1({immediate_decoder_1_u, {12{1'b0}}}), .out(multiplexer_3_out), .sel(LUI));  // open: en
  Multiplexer #(.width(32)) multiplexer_4 (
    .in0(multiplexer_5_out), .in1(adder_3_out), .out(multiplexer_4_out), .sel(AUIPC));  // open: en
  Multiplexer #(.width(32)) multiplexer_5 (
    .in0(ALU_out_6), .in1(adder_4_out), .out(multiplexer_5_out), .sel(or_2_out));  // open: en
  register_write register_write_1 (.in_1(opcode), .out_2(register_write_1_out_2));
  Comparator #(.width(5), .mode("unsigned")) comparator_1 (
    .a({5{1'b0}}), .b(multiplexer_1_out), .eq(comparator_1_eq));  // open: gt, lt
  Comparator #(.width(5), .mode("unsigned")) comparator_2 (
    .a({5{1'b0}}), .b(multiplexer_2_out), .eq(comparator_2_eq));  // open: gt, lt
  or or_2 (or_2_out, JAL, JALR);
  RAM #(.addrWidth(5), .dataWidth(32), .bus("separate")) ram_1 (
    .addr(multiplexer_1_out), .din(multiplexer_3_out), .data(ram_1_data), .str(register_write_1_out_2),
    .clk(not_8_out), .ld(1'b1));  // open: sel, clr
  RAM #(.addrWidth(5), .dataWidth(32), .bus("separate")) ram_2 (
    .addr(multiplexer_2_out), .din(multiplexer_3_out), .data(ram_2_data), .str(register_write_1_out_2),
    .clk(not_8_out), .ld(1'b1));  // open: sel, clr
  Multiplexer #(.width(32)) multiplexer_6 (
    .in0(ram_1_data), .in1({32{1'b0}}), .out(multiplexer_6_out), .sel(comparator_1_eq));  // open: en
  Multiplexer #(.width(32)) multiplexer_7 (
    .in0(ram_2_data), .in1({32{1'b0}}), .out(multiplexer_7_out), .sel(comparator_2_eq));  // open: en
  Register #(.width(32), .trigger("high")) register_1 (
    .D(multiplexer_6_out), .Q(register_1_q), .clk(not_4_out));  // open: en, clr
  Register #(.width(32), .trigger("high")) register_2 (
    .D(multiplexer_7_out), .Q(register_2_q), .clk(not_4_out));  // open: en, clr
  Comparator #(.width(7), .mode("unsigned")) comparator_3 (
    .a(7'b0010011), .b(opcode), .eq(comparator_3_eq));  // open: gt, lt
  branch_evaluator branch_evaluator (
    .rs1(register_1_q), .rs2(register_2_q), .funct3(funct3), .out_4(branch_evaluator_out_4));
  Comparator #(.width(7), .mode("unsigned")) comparator_4 (
    .a(7'b1100011), .b(opcode), .eq(comparator_4_eq));  // open: gt, lt
  and and_2 (and_2_out, comparator_4_eq, branch_evaluator_out_4);
  Multiplexer #(.width(32)) multiplexer_8 (
    .in0(register_2_q), .in1(I_immediate_32b), .out(multiplexer_8_out), .sel(comparator_3_eq));  // open: en
  Bit_Extender #(.in_width(32), .out_width(24)) bit_extender_3 (.out(bit_extender_3_out));  // open: in
  ALU ALU (
    .rs1(register_1_q), .rs2(multiplexer_8_out), .immediate(comparator_3_eq), .funct7_i_think(funct7),
    .funct3(funct3), .out_6(ALU_out_6));
  RAM #(.addrWidth(24), .dataWidth(32), .bus("separate")) ram_3 (.addr(bit_extender_3_out));  // open: din, data, str, sel, clk, ld, clr

  // Notes on the sheet:
  //   splitter discards 2 least significant and 6 most significant bits
  //   control state B
  //   control state A
  //   contents of rom_1 (hex, n*v repeats v):
  //   16413*0 1737 793 513 800813 39d70893 3e800593 17f713 fcd78693 b7f613 70463 61463 f50533 178793
  //   d87663 feb790e3 8067 1150533 fcb79ae3 ff5ff06f 2197 1a818193 80c18513 82818613 40a60633 593 27c000ef
  //   517 16850513 118000ef 1cc000ef 12503 410593 613 f7dff0ef 1140006f 8067 12537 127b7 a6850713 a6878793
  //   e78c63 337 30313 30663 a6850513 30067 8067 127b7 12537 a6878593 a6850793 40f585b3 4025d593 1f5d793
  //   b785b3 4015d593 58c63 337 30313 30663 a6850513 30067 8067 80c1c703 4071663 ff010113 812423 112623
  //   78413 f7dff0ef 7b7 78793 78a63 10537 63050513 ffff0097 e60080e7 100793 80f18623 c12083 812403
  //   1010113 8067 8067 7b7 78793 2078663 125b7 10537 ff010113 a7858593 63050513 112623 ffff0097 e18080e7
  //   c12083 1010113 f39ff06f 50593 693 613 513 2240006f ff010113 593 812423 112623 50413 28c000ef 127b7
  //   a6c7a503 3c52783 78463 780e7 40513 380000ef ff010113 117b7 11737 812423 63870713 63c78413 40e40433
  //   912223 1212023 112623 40245413 493 63c78913 941e63 812403 c12083 412483 12903 1010113 e71ff06f
  //   ffc00593 48513 370000ef a90533 ffc52783 148493 780e7 fc9ff06f ff010113 812423 912223 11437 114b7
  //   63448793 63440413 40f40433 1212023 112623 40245413 63448493 913 4891263 114b7 e11ff0ef 11437
  //   63448793 63840413 40f40433 40245413 63448493 913 2891863 c12083 812403 412483 12903 1010113 8067
  //   4a783 190913 448493 780e7 fadff06f 4a783 190913 448493 780e7 fc1ff06f f00313 50713 2c37e63 f77793
  //   a079063 8059263 ff067693 f67613 e686b3 b72023 b72223 b72423 b72623 1070713 fed766e3 61463 8067
  //   40c306b3 269693 297 5686b3 c68067 b70723 b706a3 b70623 b705a3 b70523 b704a3 b70423 b703a3 b70323
  //   b702a3 b70223 b701a3 b70123 b700a3 b70023 8067 ff5f593 859693 d5e5b3 1059693 d5e5b3 f6dff06f 279693
  //   297 5686b3 8293 fa0680e7 28093 ff078793 40f70733 f60633 f6c378e3 f3dff06f 127b7 a6c7a703 50313
  //   14872783 79663 14c70793 14f72423 47a703 1f00813 fff00513 4e84a63 271893 2030c63 1178533 8c52423
  //   1887a803 100613 e61633 c86833 1907a423 10d52423 200693 d31863 18c7a683 c6e633 18c7a623 170713 e7a223
  //   11787b3 b7a423 513 8067 fd010113 127b7 1312e23 a6c7a983 1412c23 1512a23 1612823 2112623 2812423
  //   2912223 3212023 1712623 50a93 58a13 100b13 1489a483 48c63 44a403 fff40913 241413 848433 2095863
  //   2c12083 2812403 2412483 2012903 1c12983 1812a03 1412a83 1012b03 c12b83 3010113 8067 a0c63 10442783
  //   1478863 fff90913 ffc40413 fbdff06f 44a703 442783 fff70713 3271c63 124a223 fe0780e3 1884a683 12b1733
  //   44ab83 d776b3 2069263 780e7 44a703 1489a783 f77714e3 faf48ce3 f61ff06f 42223 fcdff06f 18c4a683
  //   8442583 d77733 71863 a8513 780e7 fcdff06f 58513 780e7 fc1ff06f 593 613 693 713 793 5d00893 73
  //   2055263 ff010113 812423 50413 112623 40800433 10000ef 852023 6f 6f 8081a503 8067 50613 513 15f693
  //   68463 c50533 15d593 161613 fe0596e3 8067
  //   add 2 bits on the bottom, and 6 on the top
  //   branch evaluator output
  //   rs1 + sign extended I-immediate for JALR instruction
  //   no need to set LSB to zero as bottom 2 bits will be discarded anyway
  //   JAL and JALR both write PC+4 to rd
  //   rs1 line to to add to sign extended I-immediate for JALR instruction
  //   branch is opcode 1100011
endmodule

module immediate_decoder (
  input  [31:0] in_1,
  output [4:0] rd,
  output [4:0] rs1,
  output [6:0] opcode,
  output [4:0] rs2,
  output [2:0] funct3,
  output [6:0] funct7,
  output [11:0] I,
  output [11:0] S,
  output [12:0] B,
  output [19:0] U,
  output [31:0] J
);

  assign J = {{11{in_1[31]}}, {in_1[31], in_1[19:12], in_1[20], in_1[30:21], 1'b0}};  // Bit_Extender bit_extender_1

  assign B = {in_1[31], in_1[7], in_1[30:25], in_1[11:8], 1'b0};
  assign funct3 = in_1[14:12];
  assign funct7 = in_1[31:25];
  assign I = in_1[31:20];
  assign opcode = in_1[6:0];
  assign rd = in_1[11:7];
  assign rs1 = in_1[19:15];
  assign rs2 = in_1[24:20];
  assign S = {in_1[31:25], in_1[11:7]};
  assign U = in_1[31:12];
endmodule

module jump_evaluator (
  input  [23:0] current_program_counter,
  input  [31:0] relative_J_immediate,
  input  ALU_conditional,
  output [23:0] next_program_counter_value
);
endmodule

module ALU (
  input  [6:0] funct7_i_think,
  input  [31:0] rs1,
  input  [31:0] rs2,
  input  immediate,
  input  [2:0] funct3,
  output [31:0] out_6
);

  wire and_1_out, comparator_1_gt, comparator_2_gt, not_1_out;
  wire [31:0] adder_1_out, and_2_out, bit_extender_1_out, bit_extender_2_out, multiplexer_1_out,
       multiplexer_2_out, or_1_out, shifter_1_out, shifter_2_out, shifter_3_out, subtractor_1_out, xor_1_out;

  not not_1 (not_1_out, immediate);
  Adder #(.width(32)) adder_1 (.a(rs2), .b(rs1), .out(adder_1_out));  // open: cin, cout
  Subtractor #(.width(32)) subtractor_1 (.a(rs2), .b(rs1), .out(subtractor_1_out));  // open: bin, bout
  Shifter #(.width(32)) shifter_1 (.in(rs2), .\dist (rs1[4:0]), .out(shifter_1_out));
  Comparator #(.width(32)) comparator_1 (.a(rs2), .b(rs1), .gt(comparator_1_gt));  // open: eq, lt
  Comparator #(.width(32), .mode("unsigned")) comparator_2 (.a(rs2), .b(rs1), .gt(comparator_2_gt));  // open: eq, lt
  Shifter #(.width(32), .shift("lr")) shifter_2 (.in(rs2), .\dist (rs1[4:0]), .out(shifter_2_out));
  Shifter #(.width(32), .shift("ar")) shifter_3 (.in(rs2), .\dist (rs1[4:0]), .out(shifter_3_out));
  Multiplexer #(.width(32)) multiplexer_1 (
    .in0(adder_1_out), .in1(subtractor_1_out), .out(multiplexer_1_out), .sel(and_1_out));  // open: en
  and and_1 (and_1_out, not_1_out, funct7_i_think[5]);
  assign xor_1_out = rs2 ^ rs1;  // XOR_Gate xor_1, 32 bits wide
  Multiplexer #(.width(32)) multiplexer_2 (
    .in0(shifter_2_out), .in1(shifter_3_out), .out(multiplexer_2_out), .sel(funct7_i_think[5]));  // open: en
  assign or_1_out = rs2 | rs1;  // OR_Gate or_1, 32 bits wide
  assign and_2_out = rs2 & rs1;  // AND_Gate and_2, 32 bits wide
  assign bit_extender_1_out = {{31{1'b0}}, comparator_1_gt};  // Bit_Extender bit_extender_1
  assign bit_extender_2_out = {{31{1'b0}}, comparator_2_gt};  // Bit_Extender bit_extender_2
  Multiplexer #(.select(3), .width(32)) multiplexer_3 (
    .in0(multiplexer_1_out), .in1(shifter_1_out), .in2(bit_extender_1_out), .in3(bit_extender_2_out),
    .in4(xor_1_out), .in5(multiplexer_2_out), .in6(or_1_out), .in7(and_2_out), .out(out_6), .sel(funct3));  // open: en

  // Notes on the sheet:
  //   ADD
  //   SUB
  //   SLL
  //   SLT
  //   SLTU
  //   XOR
  //   SRL
  //   SRA
  //   OR
  //   AND
  //   bit 5 of funct7 is used a lot
  //   on if rs1 < rs2
endmodule

module immediate_chooser (
  input  [6:0] opcode,
  input  [2:0] funct3,
  output I,
  output R,
  output S,
  output B,
  output U,
  output J
);

  wire comparator_1_eq, comparator_2_eq, comparator_3_eq, comparator_4_eq, comparator_5_eq, comparator_6_eq,
       comparator_9_eq, comparator_10_eq, demultiplexer_1_out0, demultiplexer_1_out1, or_1_out;

  Comparator #(.width(3)) comparator_1 (.a(funct3), .b(3'b001), .eq(comparator_1_eq));  // open: gt, lt
  Comparator #(.width(3)) comparator_2 (.a(funct3), .b(3'b101), .eq(comparator_2_eq));  // open: gt, lt
  or or_1 (or_1_out, comparator_1_eq, comparator_2_eq);
  Comparator #(.width(5)) comparator_3 (.a(opcode[6:2]), .b({5{1'b0}}), .eq(comparator_3_eq));  // open: gt, lt
  Comparator #(.width(5)) comparator_4 (.a(opcode[6:2]), .b(5'b00100), .eq(comparator_4_eq));  // open: gt, lt
  Demultiplexer demultiplexer_1 (
    .out0(demultiplexer_1_out0), .out1(demultiplexer_1_out1), .in(comparator_4_eq), .sel(or_1_out));  // open: en
  Comparator #(.width(5)) comparator_5 (.a(opcode[6:2]), .b(5'b11001), .eq(comparator_5_eq));  // open: gt, lt
  Comparator #(.width(5)) comparator_6 (.a(opcode[6:2]), .b(5'b01100), .eq(comparator_6_eq));  // open: gt, lt
  Comparator #(.width(5)) comparator_7 (.a(opcode[6:2]), .b(5'b01000), .eq(S));  // open: gt, lt
  Comparator #(.width(5)) comparator_8 (.a(opcode[6:2]), .b(5'b11000), .eq(B));  // open: gt, lt
  Comparator #(.width(5)) comparator_9 (.a(opcode[6:2]), .b(5'b01101), .eq(comparator_9_eq));  // open: gt, lt
  Comparator #(.width(5)) comparator_10 (.a(opcode[6:2]), .b(5'b00101), .eq(comparator_10_eq));  // open: gt, lt
  Comparator #(.width(5)) comparator_11 (.a(opcode[6:2]), .b(5'b11011), .eq(J));  // open: gt, lt
  or or_2 (I, comparator_3_eq, demultiplexer_1_out0, comparator_5_eq);
  or or_3 (R, demultiplexer_1_out1, comparator_6_eq);
  or or_4 (U, comparator_9_eq, comparator_10_eq);
endmodule

module branch_evaluator (
  input  [31:0] rs1,
  input  [31:0] rs2,
  input  [2:0] funct3,
  output out_4
);

  wire comparator_1_eq, comparator_1_lt, comparator_2_gt, multiplexer_1_out, undriven;

  Comparator #(.width(32)) comparator_1 (.a(rs1), .b(rs2), .eq(comparator_1_eq), .lt(comparator_1_lt));  // open: gt
  Comparator #(.width(32), .mode("unsigned")) comparator_2 (.a(rs2), .b(rs1), .gt(comparator_2_gt));  // open: eq, lt
  Multiplexer #(.select(2)) multiplexer_1 (
    .in0(comparator_1_eq), .in1(comparator_1_lt), .in2(comparator_1_lt), .in3(comparator_2_gt),
    .out(multiplexer_1_out), .sel(funct3[2:1]), .en(undriven));
  xor xor_1 (out_4, multiplexer_1_out, funct3[0]);

  // Notes on the sheet:
  //   NOTE: 010 and 011 are invalid funct3 values for branch. they are treated as if they were 100 and 101
  //   least significant bit of funct3 inverts branch
endmodule

module LUI_AUIPC_JAL_JALR (
  input  [6:0] in_1,
  output JALR,
  output JAL,
  output AUIPC,
  output LUI
);

  Comparator #(.width(7)) comparator_1 (.a(7'b1100111), .b(in_1), .eq(JALR));  // open: gt, lt
  Comparator #(.width(7)) comparator_2 (.a(7'b1101111), .b(in_1), .eq(JAL));  // open: gt, lt
  Comparator #(.width(7)) comparator_3 (.a(7'b0010111), .b(in_1), .eq(AUIPC));  // open: gt, lt
  Comparator #(.width(7)) comparator_4 (.a(7'b0110111), .b(in_1), .eq(LUI));  // open: gt, lt
endmodule

module register_write (
  input  [6:0] in_1,
  output out_2
);

  wire comparator_1_eq, comparator_2_eq, comparator_3_eq, comparator_4_eq, comparator_5_eq, comparator_6_eq;

  Comparator #(.width(7)) comparator_1 (.a(7'b1100111), .b(in_1), .eq(comparator_1_eq));  // open: gt, lt
  Comparator #(.width(7)) comparator_2 (.a(7'b1101111), .b(in_1), .eq(comparator_2_eq));  // open: gt, lt
  Comparator #(.width(7)) comparator_3 (.a(7'b0010111), .b(in_1), .eq(comparator_3_eq));  // open: gt, lt
  Comparator #(.width(7)) comparator_4 (.a(7'b0110111), .b(in_1), .eq(comparator_4_eq));  // open: gt, lt
  Comparator #(.width(7), .mode("unsigned")) comparator_5 (
    .a(7'b0010011), .b(in_1), .eq(comparator_5_eq));  // open: gt, lt
  Comparator #(.width(7), .mode("unsigned")) comparator_6 (
    .a(7'b0110011), .b(in_1), .eq(comparator_6_eq));  // open: gt, lt
  or or_1 (out_2, comparator_1_eq, comparator_2_eq, comparator_3_eq, comparator_4_eq, comparator_5_eq, comparator_6_eq);

  // Notes on the sheet:
  //   0110111, 0010111, 1101111, 1100111, 0010011, 0110011 all write to registers
endmodule
